# Fritzing sketch LDR (saved by Fritzing 0.9.3b)
breadboards: 1

parts:
  Part2 = Arduino Uno (Rev3)
  R1 = Resistor [tolerance=±5% resistance=10k package="0402 [SMD]"]
  R2 = Photocell (LDR) [package=THT]

nets:
  N1: Part2.A5/SCL, R1.Pin_1, R2.pin_0
  N2: Part2.5V, R2.pin_1
  N3: Part2.GND, R1.Pin_0
