# Fritzing sketch LEDServer (saved by Fritzing 0.9.3b)
breadboards: 1

parts:
  LED1 = smd LED [color="Red (633nm)" package="0805 [SMD]"]
  R1 = Resistor [tolerance=±5% resistance=300 package="0402 [SMD]"]
  Part2 = Arduino Uno (Rev3)

nets:
  N1: LED1.cathode, R1.Pin_1
  N2: LED1.anode, Part2.D6_PWM
  N3: R1.Pin_0, Part2.GND
