# Fritzing sketch LM35fzz (saved by Fritzing 0.9.3b)
breadboards: 1

parts:
  Part2 = Arduino Uno (Rev3)
  T1 = LM35 Temperature Sensor [package="TO92 [THT]"]

nets:
  N1: Part2.A1, T1.Vout
  N2: Part2.5V, T1.+Vs
  GND: Part2.GND, T1.GND
