# Fritzing sketch Potentiometer (saved by Fritzing 0.9.3b)
breadboards: 1

parts:
  Part2 = Arduino Uno (Rev3)
  U1 = POT [package=pot_mammoth]

nets:
  N1: Part2.A0, U1.A
  N2: Part2.5V, U1.E
  N3: Part2.GND, U1.S
