# Fritzing sketch PotentiometerLEDAnalog (saved by Fritzing 0.9.3b)
breadboards: 1

parts:
  Part2 = Arduino Uno (Rev3)
  U1 = POT [package=pot_mammoth]
  LED1 = LED - 5mm [color="Red (633nm)" package="5 mm [THT]"]
  R1 = Resistor [tolerance=±5% resistance=300 package=THT]

nets:
  N1: Part2.A0, U1.A
  N2: Part2.D9_PWM, LED1.anode
  N3: Part2.5V, U1.E
  N4: Part2.GND, U1.S, R1.Pin_0
  N5: LED1.cathode, R1.Pin_1
