# Fritzing sketch Pushbutton (saved by Fritzing 0.9.3b)
breadboards: 1

parts:
  Part2 = Arduino Uno (Rev3)
  S1 = Pushbutton [package="[THT]"]
  R2 = Resistor [tolerance=±5% resistance=10k package=THT]

nets:
  N1: Part2.D2, S1.Pin_3, S1.Pin_4, R2.Pin_1
  N2: Part2.5V, S1.Pin_1, S1.Pin_2
  N3: Part2.GND, R2.Pin_0
