# Fritzing sketch PushbuttonLED (saved by Fritzing 0.9.3b)
breadboards: 1

parts:
  Part2 = Arduino Uno (Rev3)
  R1 = Resistor [tolerance=±5% resistance=300 package="0402 [SMD]"]
  LED1 = smd LED [color="Red (633nm)" package="0805 [SMD]"]
  S1 = Pushbutton [package="[THT]"]
  R2 = Resistor [tolerance=±5% resistance=10k package=THT]

nets:
  N1: Part2.D13/SCK, LED1.anode
  N2: Part2.D2, S1.Pin_3, S1.Pin_4, R2.Pin_1
  N3: Part2.5V, S1.Pin_1, S1.Pin_2
  N4: Part2.GND, R1.Pin_0, R2.Pin_0
  N5: R1.Pin_1, LED1.cathode
