# Fritzing sketch ServoControl (saved by Fritzing 0.9.3b)
breadboards: 1

parts:
  Part2 = Arduino Uno (Rev3)
  SERVO1 = Tower Pro SG90 servo [part_number=101246]
  U1 = POT [package=pot_mammoth]

nets:
  N1: Part2.A0, U1.A
  N2: Part2.D9_PWM, SERVO1.Signal
  5V: Part2.5V, SERVO1.+5V, U1.E
  GND: Part2.GND, SERVO1.GND, U1.S

custom parts:
  Tower Pro SG90 servo: Original file by John De Cristofaro http://www.adafruit.com/products/1449 Adafruit Feedback Servo (Small) Edited by: e-radionica.com 28/9/2015
