# Fritzing sketch Ultrassonic (saved by Fritzing 0.9.3b)
breadboards: 1

parts:
  Part2 = Arduino Uno (Rev3)
  Part3 = SRF05 Ultrasonic Rangefinder

nets:
  N1: Part2.D8, Part3.Trig
  N2: Part2.D7, Part3.Echo
  5V: Part2.5V, Part3.VCC
  GND: Part2.GND, Part3.GND
